// Logisim project Logic Circuits (Adder & Logic Gates).circ as structural Verilog: 18 circuits, main circuit main
module main (
  input  in_1,
  input  in_2,
  input  in_3,
  output out_4
);

  wire and_1_out_3, and_2_out_3, nor_1_out_3, not_1_out_2, not_2_out_2, not_3_out_2, or_1_out_3;

  NOT not_1 (.in_1(in_3), .out_2(not_1_out_2));
  NOR nor_1 (.in_1(in_1), .in_2(not_1_out_2), .out_3(nor_1_out_3));
  NOT not_2 (.in_1(in_1), .out_2(not_2_out_2));
  OR or_1 (.in_1(not_2_out_2), .in_2(not_3_out_2), .out_3(or_1_out_3));
  NOT not_3 (.in_1(in_2), .out_2(not_3_out_2));
  AND and_1 (.in_1(not_3_out_2), .in_2(in_3), .out_3(and_1_out_3));
  AND and_2 (.in_1(nor_1_out_3), .in_2(or_1_out_3), .out_3(and_2_out_3));
  AND and_3 (.in_1(and_2_out_3), .in_2(and_1_out_3), .out_3(out_4));
endmodule

module AND (
  input  in_1,
  input  in_2,
  output out_3
);

  wire transistor_1_out, transistor_3_out;

  Transistor transistor_1 (.in(1'b1), .out(transistor_1_out), .gate(in_1));
  Transistor #(.\type ("n")) transistor_2 (.in(transistor_3_out), .out(transistor_1_out), .gate(in_1));
  Transistor #(.\type ("n")) transistor_3 (.in(1'b0), .out(transistor_3_out), .gate(in_2));
  Transistor transistor_4 (.in(1'b1), .out(transistor_1_out), .gate(in_2));
  Transistor transistor_5 (.in(1'b1), .out(out_3), .gate(transistor_1_out));
  Transistor #(.\type ("n")) transistor_6 (.in(1'b0), .out(out_3), .gate(transistor_1_out));

  // Notes on the sheet:
  //   AND Gate
endmodule

module NAND (
  input  in_1,
  input  in_2,
  output out_3
);

  wire transistor_4_out;

  Transistor transistor_1 (.in(1'b1), .out(out_3), .gate(in_1));
  Transistor transistor_2 (.in(1'b1), .out(out_3), .gate(in_2));
  Transistor #(.\type ("n")) transistor_3 (.in(transistor_4_out), .out(out_3), .gate(in_1));
  Transistor #(.\type ("n")) transistor_4 (.in(1'b0), .out(transistor_4_out), .gate(in_2));

  // Notes on the sheet:
  //   NAND Gate
endmodule

module OR (
  input  in_1,
  input  in_2,
  output out_3
);

  wire transistor_3_out;

  Transistor #(.\type ("n")) transistor_1 (.in(1'b1), .out(out_3), .gate(in_1));
  Transistor transistor_2 (.in(transistor_3_out), .out(out_3), .gate(in_1));
  Transistor transistor_3 (.in(1'b0), .out(transistor_3_out), .gate(in_2));
  Transistor #(.\type ("n")) transistor_4 (.in(1'b1), .out(out_3), .gate(in_2));

  // Notes on the sheet:
  //   OR Gate
endmodule

module NOR (
  input  in_1,
  input  in_2,
  output out_3
);

  wire transistor_1_out, transistor_4_out;

  Transistor #(.\type ("n")) transistor_1 (.in(1'b1), .out(transistor_1_out), .gate(in_2));
  Transistor #(.\type ("n")) transistor_2 (.in(1'b1), .out(transistor_1_out), .gate(in_1));
  Transistor transistor_3 (.in(transistor_4_out), .out(transistor_1_out), .gate(in_1));
  Transistor transistor_4 (.in(1'b0), .out(transistor_4_out), .gate(in_2));
  Transistor transistor_5 (.in(1'b1), .out(out_3), .gate(transistor_1_out));
  Transistor #(.\type ("n")) transistor_6 (.in(1'b0), .out(out_3), .gate(transistor_1_out));

  // Notes on the sheet:
  //   NOR Gate
endmodule

module XOR (
  input  in_1,
  input  in_2,
  output out_3
);

  wire transistor_1_out, transistor_2_out, transistor_7_out, transistor_8_out;

  Transistor transistor_1 (.in(1'b1), .out(transistor_1_out), .gate(in_1));
  Transistor #(.\type ("n")) transistor_2 (.in(1'b1), .out(transistor_2_out), .gate(in_1));
  Transistor #(.\type ("n")) transistor_3 (.in(transistor_1_out), .out(out_3), .gate(in_2));
  Transistor transistor_4 (.in(transistor_2_out), .out(out_3), .gate(in_2));
  Transistor transistor_5 (.in(transistor_8_out), .out(out_3), .gate(in_1));
  Transistor #(.\type ("n")) transistor_6 (.in(transistor_7_out), .out(out_3), .gate(in_1));
  Transistor #(.\type ("n")) transistor_7 (.in(1'b0), .out(transistor_7_out), .gate(in_2));
  Transistor transistor_8 (.in(1'b0), .out(transistor_8_out), .gate(in_2));

  // Notes on the sheet:
  //   XOR Gate
endmodule

module NOT (
  input  in_1,
  output out_2
);

  Transistor transistor_1 (.in(1'b1), .out(out_2), .gate(in_1));
  Transistor #(.\type ("n")) transistor_2 (.in(1'b0), .out(out_2), .gate(in_1));

  // Notes on the sheet:
  //   NOT Gate
endmodule

module Half_Adder (
  input  A,
  input  B,
  output C_out,
  output Output
);

  AND and_1 (.in_1(A), .in_2(B), .out_3(C_out));
  XOR xor_1 (.in_1(A), .in_2(B), .out_3(Output));
endmodule

module Full_Adder (
  input  A,
  input  B,
  input  C_in,
  output C_out,
  output Output
);

  wire half_adder_1_c_out, half_adder_1_output, half_adder_2_c_out;

  Half_Adder half_adder_1 (.A(A), .B(B), .C_out(half_adder_1_c_out), .Output(half_adder_1_output));
  Half_Adder half_adder_2 (.A(half_adder_1_output), .B(C_in), .C_out(half_adder_2_c_out), .Output(Output));
  OR or_1 (.in_1(half_adder_1_c_out), .in_2(half_adder_2_c_out), .out_3(C_out));
endmodule

module _4_bit_Full_Adder (
  input  _1st_num,
  input  in_2,
  input  in_3,
  input  in_4,
  input  in_5,
  input  in_6,
  input  in_7,
  input  in_8,
  output Output,
  output out_10,
  output out_11,
  output out_12,
  output out_13
);

  wire full_adder_2_c_out, full_adder_3_c_out, half_adder_1_c_out;

  Full_Adder full_adder_1 (.A(_1st_num), .B(in_2), .C_in(full_adder_2_c_out), .C_out(Output), .Output(out_10));
  Full_Adder full_adder_2 (.A(in_3), .B(in_4), .C_in(full_adder_3_c_out), .C_out(full_adder_2_c_out), .Output(out_11));
  Full_Adder full_adder_3 (.A(in_5), .B(in_6), .C_in(half_adder_1_c_out), .C_out(full_adder_3_c_out), .Output(out_12));
  Half_Adder half_adder_1 (.A(in_7), .B(in_8), .C_out(half_adder_1_c_out), .Output(out_13));

  // Notes on the sheet:
  //   2nd #
endmodule

module _4_bit_Substractor (
  input  _1st_num,
  input  in_2,
  input  in_3,
  input  in_4,
  input  in_5,
  input  in_6,
  input  in_7,
  input  in_8,
  output Output,
  output out_10,
  output out_11,
  output out_12,
  output out_13
);

  wire full_adder_2_c_out, full_adder_3_c_out, full_adder_4_c_out, not_1_out_2, not_2_out_2, not_3_out_2,
       not_4_out_2;

  NOT not_1 (.in_1(in_2), .out_2(not_1_out_2));
  NOT not_2 (.in_1(in_4), .out_2(not_2_out_2));
  NOT not_3 (.in_1(in_6), .out_2(not_3_out_2));
  NOT not_4 (.in_1(in_8), .out_2(not_4_out_2));
  Full_Adder full_adder_1 (.A(_1st_num), .B(not_1_out_2), .C_in(full_adder_2_c_out), .C_out(Output), .Output(out_10));
  Full_Adder full_adder_2 (
    .A(in_3), .B(not_2_out_2), .C_in(full_adder_3_c_out), .C_out(full_adder_2_c_out), .Output(out_11));
  Full_Adder full_adder_3 (
    .A(in_5), .B(not_3_out_2), .C_in(full_adder_4_c_out), .C_out(full_adder_3_c_out), .Output(out_12));
  Full_Adder full_adder_4 (.A(in_7), .B(not_4_out_2), .C_in(1'b1), .C_out(full_adder_4_c_out), .Output(out_13));

  // Notes on the sheet:
  //   2nd #
endmodule

module Mux (
  input  Sub,
  input  plus_ve,
  input  minus_ve,
  output out_4
);

  Transistor transistor_1 (.in(plus_ve), .out(out_4), .gate(Sub));
  Transistor #(.\type ("n")) transistor_2 (.in(minus_ve), .out(out_4), .gate(Sub));
endmodule

module _4_bit_Adder_Substractor (
  input  sub,
  input  _1st_num,
  input  in_3,
  input  in_4,
  input  in_5,
  input  in_6,
  input  in_7,
  input  in_8,
  input  in_9,
  output Overflow,
  output Output,
  output out_12,
  output out_13,
  output out_14
);

  wire full_adder_1_c_out, full_adder_2_c_out, full_adder_3_c_out, full_adder_4_c_out, mux_1_out_4,
       mux_2_out_4, mux_3_out_4, mux_4_out_4, not_1_out_2, not_2_out_2, not_3_out_2, not_4_out_2;

  NOT not_1 (.in_1(in_3), .out_2(not_1_out_2));
  NOT not_2 (.in_1(in_5), .out_2(not_2_out_2));
  NOT not_3 (.in_1(in_7), .out_2(not_3_out_2));
  NOT not_4 (.in_1(in_9), .out_2(not_4_out_2));
  Mux mux_1 (.Sub(sub), .plus_ve(in_3), .minus_ve(not_1_out_2), .out_4(mux_1_out_4));
  Mux mux_2 (.Sub(sub), .plus_ve(in_5), .minus_ve(not_2_out_2), .out_4(mux_2_out_4));
  Mux mux_3 (.Sub(sub), .plus_ve(in_7), .minus_ve(not_3_out_2), .out_4(mux_3_out_4));
  Mux mux_4 (.Sub(sub), .plus_ve(in_9), .minus_ve(not_4_out_2), .out_4(mux_4_out_4));
  XOR xor_1 (.in_1(full_adder_2_c_out), .in_2(full_adder_1_c_out), .out_3(Overflow));
  Full_Adder full_adder_1 (
    .A(_1st_num), .B(mux_1_out_4), .C_in(full_adder_2_c_out), .C_out(full_adder_1_c_out), .Output(Output));
  Full_Adder full_adder_2 (
    .A(in_4), .B(mux_2_out_4), .C_in(full_adder_3_c_out), .C_out(full_adder_2_c_out), .Output(out_12));
  Full_Adder full_adder_3 (
    .A(in_6), .B(mux_3_out_4), .C_in(full_adder_4_c_out), .C_out(full_adder_3_c_out), .Output(out_13));
  Full_Adder full_adder_4 (.A(in_8), .B(mux_4_out_4), .C_in(sub), .C_out(full_adder_4_c_out), .Output(out_14));

  // Notes on the sheet:
  //   Sub?
  //   2nd #
endmodule

module _7_seg (
  input  Sub,
  input  _1,
  input  _2,
  input  in_4,
  input  in_5,
  input  in_6,
  input  in_7,
  input  in_8,
  input  in_9
);

  wire and_1_out_3, and_2_out_3, and_3_out_3, and_4_out_3, and_5_out_3, and_6_out_3, and_7_out_3,
       and_8_out_3, and_9_out_3, and_10_out_3, and_11_out_3, and_12_out_3, and_13_out_3, and_14_out_3,
       and_15_out_3, and_16_out_3, and_17_out_3, and_18_out_3, and_19_out_3, and_20_out_3, and_21_out_3,
       and_22_out_3, n4_bit_adder_substractor_1_out_12, n4_bit_adder_substractor_1_out_13,
       n4_bit_adder_substractor_1_out_14, n4_bit_adder_substractor_1_output,
       n4_bit_adder_substractor_1_overflow, not_1_out_2, not_2_out_2, not_3_out_2, not_4_out_2, or_1_out_3,
       or_2_out_3, or_3_out_3, or_4_out_3, or_5_out_3, or_6_out_3, or_7_out_3, or_8_out_3, or_9_out_3,
       or_10_out_3, or_11_out_3, or_12_out_3, or_13_out_3, or_14_out_3, or_15_out_3, or_16_out_3,
       or_17_out_3, or_18_out_3, or_19_out_3, or_20_out_3, or_21_out_3, undriven, undriven_2, undriven_3,
       undriven_4, xor_2_out_3, xor_3_out_3;

  AND and_1 (.in_1(n4_bit_adder_substractor_1_out_12), .in_2(n4_bit_adder_substractor_1_output), .out_3(and_1_out_3));
  AND and_2 (.in_1(not_1_out_2), .in_2(not_3_out_2), .out_3(and_2_out_3));
  AND and_3 (.in_1(not_2_out_2), .in_2(n4_bit_adder_substractor_1_out_13), .out_3(and_3_out_3));
  AND and_4 (.in_1(n4_bit_adder_substractor_1_out_13), .in_2(not_4_out_2), .out_3(and_4_out_3));
  AND and_5 (.in_1(not_1_out_2), .in_2(n4_bit_adder_substractor_1_out_13), .out_3(and_5_out_3));
  XOR xor_1 (.in_1(n4_bit_adder_substractor_1_output), .in_2(n4_bit_adder_substractor_1_out_12));  // open: out_3
  AND and_6 (.in_1(not_1_out_2), .in_2(n4_bit_adder_substractor_1_out_12), .out_3(and_6_out_3));
  AND and_7 (.in_1(n4_bit_adder_substractor_1_out_12), .in_2(not_3_out_2), .out_3(and_7_out_3));
  XOR xor_2 (.in_1(n4_bit_adder_substractor_1_out_12), .in_2(n4_bit_adder_substractor_1_out_13), .out_3(xor_2_out_3));
  AND and_8 (.in_1(not_1_out_2), .in_2(not_2_out_2), .out_3(and_8_out_3));
  AND and_9 (.in_1(not_2_out_2), .in_2(n4_bit_adder_substractor_1_output), .out_3(and_9_out_3));
  AND and_10 (.in_1(n4_bit_adder_substractor_1_output), .in_2(not_3_out_2), .out_3(and_10_out_3));
  AND and_11 (.in_1(not_3_out_2), .in_2(n4_bit_adder_substractor_1_out_14), .out_3(and_11_out_3));
  AND and_12 (.in_1(not_4_out_2), .in_2(and_7_out_3), .out_3(and_12_out_3));
  AND and_13 (.in_1(n4_bit_adder_substractor_1_out_13), .in_2(and_9_out_3), .out_3(and_13_out_3));
  AND and_14 (.in_1(not_4_out_2), .in_2(and_8_out_3), .out_3(and_14_out_3));
  AND and_15 (.in_1(and_7_out_3), .in_2(n4_bit_adder_substractor_1_out_14), .out_3(and_15_out_3));
  AND and_16 (.in_1(n4_bit_adder_substractor_1_out_14), .in_2(and_9_out_3), .out_3(and_16_out_3));
  AND and_17 (.in_1(and_4_out_3), .in_2(n4_bit_adder_substractor_1_output), .out_3(and_17_out_3));
  AND and_18 (.in_1(and_6_out_3), .in_2(n4_bit_adder_substractor_1_out_13), .out_3(and_18_out_3));
  AND and_19 (.in_1(and_9_out_3), .in_2(and_11_out_3), .out_3(and_19_out_3));
  AND and_20 (.in_1(and_2_out_3), .in_2(not_4_out_2), .out_3(and_20_out_3));
  _4_bit_Adder_Substractor u_4_bit_adder_substractor_1 (
    .sub(Sub), ._1st_num(_1), .in_3(_2), .in_4(in_4), .in_5(in_5), .in_6(in_6), .in_7(in_7), .in_8(in_8),
    .in_9(in_9), .Overflow(n4_bit_adder_substractor_1_overflow), .Output(n4_bit_adder_substractor_1_output),
    .out_12(n4_bit_adder_substractor_1_out_12), .out_13(n4_bit_adder_substractor_1_out_13),
    .out_14(n4_bit_adder_substractor_1_out_14));
  NOT not_1 (.in_1(n4_bit_adder_substractor_1_output), .out_2(not_1_out_2));
  AND and_21 (.in_1(not_3_out_2), .in_2(not_4_out_2), .out_3(and_21_out_3));
  AND and_22 (.in_1(n4_bit_adder_substractor_1_out_14), .in_2(and_5_out_3), .out_3(and_22_out_3));
  NOT not_2 (.in_1(n4_bit_adder_substractor_1_out_12), .out_2(not_2_out_2));
  OR or_1 (.in_1(and_16_out_3), .in_2(and_13_out_3), .out_3(or_1_out_3));
  OR or_2 (.in_1(and_12_out_3), .in_2(and_6_out_3), .out_3(or_2_out_3));
  OR or_3 (.in_1(and_19_out_3), .in_2(and_18_out_3), .out_3(or_3_out_3));
  OR or_4 (.in_1(or_3_out_3), .in_2(or_5_out_3), .out_3(or_4_out_3));
  OR or_5 (.in_1(and_14_out_3), .in_2(and_17_out_3), .out_3(or_5_out_3));
  OR or_6 (.in_1(n4_bit_adder_substractor_1_out_14), .in_2(not_3_out_2), .out_3(or_6_out_3));
  OR or_7 (.in_1(or_6_out_3), .in_2(xor_3_out_3), .out_3(or_7_out_3));
  XOR xor_3 (.in_1(n4_bit_adder_substractor_1_out_12), .in_2(n4_bit_adder_substractor_1_output), .out_3(xor_3_out_3));
  OR or_8 (.in_1(and_16_out_3), .in_2(or_9_out_3), .out_3(or_8_out_3));
  OR or_9 (.in_1(and_15_out_3), .in_2(and_14_out_3), .out_3(or_9_out_3));
  OR or_10 (.in_1(and_4_out_3), .in_2(and_5_out_3), .out_3(or_10_out_3));
  OR or_11 (.in_1(and_1_out_3), .in_2(and_2_out_3), .out_3(or_11_out_3));
  OR or_12 (.in_1(or_11_out_3), .in_2(or_13_out_3), .out_3(or_12_out_3));
  OR or_13 (.in_1(and_3_out_3), .in_2(and_4_out_3), .out_3(or_13_out_3));
  OR or_14 (.in_1(and_8_out_3), .in_2(and_22_out_3), .out_3(or_14_out_3));
  OR or_15 (.in_1(and_21_out_3), .in_2(and_1_out_3), .out_3(or_15_out_3));
  OR or_16 (.in_1(xor_2_out_3), .in_2(and_4_out_3), .out_3(or_16_out_3));
  OR or_17 (.in_1(and_20_out_3), .in_2(or_1_out_3), .out_3(or_17_out_3));
  OR or_18 (.in_1(or_17_out_3), .in_2(or_2_out_3), .out_3(or_18_out_3));
  OR or_19 (.in_1(or_8_out_3), .in_2(or_10_out_3), .out_3(or_19_out_3));
  NOT not_3 (.in_1(n4_bit_adder_substractor_1_out_13), .out_2(not_3_out_2));
  OR or_20 (.in_1(and_10_out_3), .in_2(or_14_out_3), .out_3(or_20_out_3));
  OR or_21 (.in_1(or_20_out_3), .in_2(or_15_out_3), .out_3(or_21_out_3));
  _7_Segment_Display u_7_segment_display_1 (.g(n4_bit_adder_substractor_1_output));  // open: f, a, b, e, d, c, dp
  _7_Segment_Display u_7_segment_display_2 (
    .g(n4_bit_adder_substractor_1_overflow), .f(n4_bit_adder_substractor_1_overflow),
    .a(n4_bit_adder_substractor_1_overflow), .e(n4_bit_adder_substractor_1_overflow),
    .d(n4_bit_adder_substractor_1_overflow));  // open: b, c, dp
  _7_Segment_Display u_7_segment_display_3 (
    .g(n4_bit_adder_substractor_1_overflow), .e(n4_bit_adder_substractor_1_overflow));  // open: f, a, b, d, c, dp
  _7_Segment_Display u_7_segment_display_4 (
    .f(or_12_out_3), .a(or_12_out_3), .b(1'b1), .e(or_12_out_3), .d(or_12_out_3), .c(1'b1));  // open: g, dp
  _7_Segment_Display u_7_segment_display_5 (
    .g(n4_bit_adder_substractor_1_overflow), .e(n4_bit_adder_substractor_1_overflow));  // open: f, a, b, d, c, dp
  NOT not_4 (.in_1(n4_bit_adder_substractor_1_out_14), .out_2(not_4_out_2));
  _7_Segment_Display u_7_segment_display_6 (
    .g(or_16_out_3), .f(or_18_out_3), .a(or_19_out_3), .b(or_21_out_3), .e(or_4_out_3), .d(or_19_out_3),
    .c(or_7_out_3));  // open: dp
  _7_Segment_Display u_7_segment_display_7 (
    .g(n4_bit_adder_substractor_1_overflow), .e(n4_bit_adder_substractor_1_overflow),
    .d(n4_bit_adder_substractor_1_overflow), .c(n4_bit_adder_substractor_1_overflow));  // open: f, a, b, dp
  _7_Segment_Display u_7_segment_display_8 (
    .g(undriven), .f(undriven_3), .b(n4_bit_adder_substractor_1_overflow), .e(undriven_2), .d(undriven_4),
    .c(n4_bit_adder_substractor_1_overflow), .dp(n4_bit_adder_substractor_1_overflow));  // open: a
  _7_Segment_Display u_7_segment_display_9 (
    .g(n4_bit_adder_substractor_1_overflow), .a(undriven), .b(undriven_3),
    .e(n4_bit_adder_substractor_1_overflow), .c(undriven_2), .dp(undriven_4));  // open: f, d

  // Notes on the sheet:
  //   AB
  //   !A!C
  //   !BC
  //   C!D
  //   !AC
  //        AxB
  //   !AB
  //   B!C
  //   BxC
  //   !A!B
  //   A!B
  //   A!B
  //   !CD
  //   B!C!D
  //   A!BC
  //   !A!B!D
  //   B!CD
  //   A!BD
  //   AC!D
  //   !ABC
  //   A!B!CD
  //   !A!C!D
  //   g f a b
  //   e d c _
  //   A
  //   !A
  //   B
  //   !C!D
  //   !ACD
  //   !B
  //   f
  //   e
  //   C
  //   #3 pin g
  //   #3 pin e
  //   #3 pin c
  //   #2 pins a & d-f
  //   a
  //   b
  //   g
  //   c
  //   d
  //   !C
  //   #3 pin f
  //   #3 pins a&d
  //   #1 pin g
  //   D
  //   #3 pin b
  //   !D
  //   #2 pins b&c
endmodule

module SR_LATCH_NOR (
  input  S,
  input  R,
  output nQ,
  output Q
);

  nor nor_1 (nQ, S, Q);
  nor nor_2 (Q, nQ, R);
endmodule

module SR_LATCH_NAND (
  input  S,
  input  R,
  output nQ,
  output Q
);

  nand nand_1 (nQ, S, Q);
  nand nand_2 (Q, nQ, R);
endmodule

module D_Latch (
  input  D,
  input  Enable,
  output Q,
  output nQ
);

  wire nand_1_out, nand_2_out, not_1_out;

  not not_1 (not_1_out, D);
  nand nand_1 (nand_1_out, D, Enable);
  nand nand_2 (nand_2_out, not_1_out, Enable);
  nand nand_3 (Q, nand_1_out, nQ);
  nand nand_4 (nQ, Q, nand_2_out);
endmodule

module D_FLIP_FLOP (
  input  D1,
  output D2,
  output Q1,
  output Q2,
  output nQ2,
  output nClock
);

  wire clock_1_out, nand_1_out, nand_2_out, nand_4_out, nand_5_out, nand_6_out, not_1_out, not_3_out;

  Clock clock_1 (.out(clock_1_out));
  not not_1 (not_1_out, D1);
  nand nand_1 (nand_1_out, D1, clock_1_out);
  nand nand_2 (nand_2_out, not_1_out, clock_1_out);
  nand nand_3 (D2, nand_1_out, nand_4_out);
  nand nand_4 (nand_4_out, D2, nand_2_out);
  not not_2 (nClock, clock_1_out);
  nand nand_5 (nand_5_out, D2, nClock);
  not not_3 (not_3_out, D2);
  nand nand_6 (nand_6_out, not_3_out, nClock);
  nand nand_7 (Q2, nand_5_out, nQ2);
  nand nand_8 (nQ2, Q2, nand_6_out);

  assign Q1 = D2;

  // Notes on the sheet:
  //   clock
endmodule
