# Fritzing sketch Radio+LED Cube (saved by Fritzing 0.9.3b)
circuit board: 10cm x 5cm
breadboards: 1

parts:
  VCC2 = Battery
  VCC1 = Battery block 9V
  U1 = LM386 [package=dip08]
  R1 = Resistor [tolerance=±5% resistance=22k package=THT]
  C1 = Electrolytic Capacitor [capacitance=470µF package="100 mil [THT, electrolytic]"]
  C2 = Ceramic Capacitor [capacitance=100nF package="100 mil [THT, multilayer]"]
  Part1 = Variable Capacitor [capacitance=100nF max_capacitance=10pF min_capacitance=2pF voltage=35V]
  Q2 = NPN-Transistor [package="TO92 [THT]"]
  Q3 = NPN-Transistor [package="TO92 [THT]"]
  C3 = Ceramic Capacitor [capacitance=100nF package="100 mil [THT, multilayer]"]
  C4 = Ceramic Capacitor [capacitance=100nF package="100 mil [THT, multilayer]"]
  C5 = Ceramic Capacitor [capacitance=100nF package="100 mil [THT, multilayer]"]
  C6 = Ceramic Capacitor [capacitance=100nF package="100 mil [THT, multilayer]"]
  R2 = TRIMPOT [package=trim_pot_pth]
  C7 = Electrolytic Capacitor [capacitance=220µF package="100 mil [THT, electrolytic]"]
  C8 = Electrolytic Capacitor [capacitance=470µF package="100 mil [THT, electrolytic]"]
  C9 = Electrolytic Capacitor [capacitance=470µF package="100 mil [THT, electrolytic]"]
  J1 = Piezo Speaker
  C10 = Electrolytic Capacitor [capacitance=470µF package="100 mil [THT, electrolytic]"]
  U2 = 555 Timer [package="DIP8 [THT]"]
  IC1 = IC, DIP package, 16 pins [chip_label=IC]
  C11 = Electrolytic Capacitor [capacitance=1µF package="100 mil [THT, electrolytic]"]
  JP1 = Header 12 [package=1x12_machine-pin-header_lock.004]
  C12 = Ceramic Capacitor [capacitance=100nF package="200 mil [THT, multilayer]"]
  R4 = TRIMPOT [package=trim_pot_pth]

nets:
  N1: VCC2.-, U1.-IN, U1.V-, C1.-, C2.0, Q2.E, Q3.E, R2.CCW, C8.-, C9.-, J1.pin1
  N2: VCC2.+, U1.V+, R1.Pin_0, C1.+, C8.+, C9.+
  N3: VCC1.-, U2.Ground, IC1.pin8, C11.-, C12.0
  N4: VCC1.+, U2.Reset, U2.Vcc_Supply_Voltage, IC1.pin16
  N5: U1.GAIN, C10.-, C10.+
  N6: U1.+IN, R2.WIPER
  N7: U1.OUT, C2.1, C7.+
  N8: R1.Pin_1, Part1.1, Q2.C, Q3.B, C3.1, C4.1, C5.1, C6.1
  N9: Part1.2, Q2.B, Q3.C
  N10: C3.0, C4.0, C5.0, C6.0, R2.CW
  N11: C7.-, J1.pin2
  N12: U2.Trigger, U2.Threshold, C11.+, R4.WIPER
  N13: IC1.pin1, JP1.12
  N14: IC1.pin4, JP1.11
  N15: IC1.pin5, JP1.9
  N16: IC1.pin6, JP1.8
  N17: IC1.pin7, JP1.7
  N18: IC1.pin10, R4.CW
  N19: IC1.pin11, C12.1
  N20: IC1.pin12, JP1.5
  N21: IC1.pin13, JP1.4
  N22: IC1.pin14, JP1.3
  N23: IC1.pin15, JP1.1
